// Digital circuit CTRLUNIT.dig as structural Verilog
module CTRLUNIT (
  input  [7:0] OPC,
  input  [2:0] microstep,
  input  Z,
  input  C,
  input  N,
  input  V,
  input  I,
  output [15:0] C0_15,
  output [15:0] C16_31,
  output [15:0] C32_47
);

  ROM #(.AddrBits(16), .Bits(16)) _1ROM (.A({I, V, N, C, Z, microstep, OPC}), .sel(1'b1), .D(C0_15));
  ROM #(.AddrBits(16), .Bits(16)) _2ROM (.A({I, V, N, C, Z, microstep, OPC}), .sel(1'b1), .D(C16_31));
  ROM #(.AddrBits(16), .Bits(16)) _3ROM (.A({I, V, N, C, Z, microstep, OPC}), .sel(1'b1), .D(C32_47));

  // Notes on the sheet:
  //   contents of _1ROM (hex, n*v repeats v):
  //   256*dda,8*cfb,8*1c3b,8*3c7b,232*cfb,1536*cfa,256*dda,8*cfb,8*1c3b
  //   ,8*3c7b,232*cfb,1536*cfa,256*dda,8*cfb,8*1c3b,8*3c7b,232*cfb,1536*cfa
  //   ,256*dda,8*cfb,8*1c3b,8*3c7b,232*cfb,1536*cfa,256*dda,8*cfb,8*1c3b
  //   ,8*3c7b,232*cfb,1536*cfa,256*dda,8*cfb,8*1c3b,8*3c7b,232*cfb,1536*cfa
  //   ,256*dda,8*cfb,8*1c3b,8*3c7b,232*cfb,1536*cfa,256*dda,8*cfb,8*1c3b
  //   ,8*3c7b,232*cfb,1536*cfa,256*dda,8*cfb,8*1c3b,8*3c7b,232*cfb,1536*cfa
  //   ,256*dda,8*cfb,8*1c3b,8*3c7b,232*cfb,1536*cfa,256*dda,8*cfb,8*1c3b
  //   ,8*3c7b,232*cfb,1536*cfa,256*dda,8*cfb,8*1c3b,8*3c7b,232*cfb,1536*cfa
  //   ,256*dda,8*cfb,8*1c3b,8*3c7b,232*cfb,1536*cfa,256*dda,8*cfb,8*1c3b
  //   ,8*3c7b,232*cfb,1536*cfa,256*dda,8*cfb,8*1c3b,8*3c7b,232*cfb,1536*cfa
  //   ,256*dda,8*cfb,8*1c3b,8*3c7b,232*cfb,1536*cfa,256*dda,8*cfb,8*1c3b
  //   ,8*3c7b,232*cfb,1536*cfa,256*dda,8*cfb,8*1c3b,8*3c7b,232*cfb,1536*cfa
  //   ,256*dda,8*cfb,8*1c3b,8*3c7b,232*cfb,1536*cfa,256*dda,8*cfb,8*1c3b
  //   ,8*3c7b,232*cfb,1536*cfa,256*dda,8*cfb,8*1c3b,8*3c7b,232*cfb,1536*cfa
  //   ,256*dda,8*cfb,8*1c3b,8*3c7b,232*cfb,1536*cfa,256*dda,8*cfb,8*1c3b
  //   ,8*3c7b,232*cfb,1536*cfa,256*dda,8*cfb,8*1c3b,8*3c7b,232*cfb,1536*cfa
  //   ,256*dda,8*cfb,8*1c3b,8*3c7b,232*cfb,1536*cfa,256*dda,8*cfb,8*1c3b
  //   ,8*3c7b,232*cfb,1536*cfa,256*dda,8*cfb,8*1c3b,8*3c7b,232*cfb,1536*cfa
  //   ,256*dda,8*cfb,8*1c3b,8*3c7b,232*cfb,1536*cfa,256*dda,8*cfb,8*1c3b
  //   ,8*3c7b,232*cfb,1536*cfa,256*dda,8*cfb,8*1c3b,8*3c7b,232*cfb,1536*cfa
  //   ,256*dda,8*cfb,8*1c3b,8*3c7b,232*cfb,1536*cfa,256*dda,8*cfb,8*1c3b
  //   ,8*3c7b,232*cfb,1536*cfa
  //   contents of _2ROM (hex, n*v repeats v):
  //   65536*b6a0
  //   contents of _3ROM (hex, n*v repeats v):
  //   65536*1e
endmodule
